// Logisim project ep1logisim.circ as structural Verilog
module meio_somador (
  input  A,
  input  B,
  output S,
  output Cout
);

  xor xor_1 (S, A, B);
  and and_1 (Cout, B, A);
endmodule

module somador_completo (
  input  Cin,
  input  A,
  input  B,
  output S,
  output Cout
);

  wire meio_somador_1_p3, meio_somador_1_p4, meio_somador_2_p4;

  // SOMADIMINUIR_meio_somador meio_somador_1: pin names not known; wires that end beside it: A, B, meio_somador_1_p3, meio_somador_1_p4
  // SOMADIMINUIR_meio_somador meio_somador_2: pin names not known; wires that end beside it: Cin, meio_somador_1_p3, S, meio_somador_2_p4
  or or_1 (Cout, meio_somador_2_p4, meio_somador_1_p4);
endmodule

module somador_subtrator_8bits (
  input  M,
  input  A0,
  input  A4,
  input  B0,
  input  B4,
  input  A1,
  input  A5,
  input  B1,
  input  B5,
  input  A2,
  input  A6,
  input  B2,
  input  B6,
  input  A3,
  input  A7,
  input  B3,
  input  B7,
  output S0,
  output S4,
  output S1,
  output S5,
  output S2,
  output S6,
  output S3,
  output S7,
  output Cout
);

  wire somador_completo_1_p5, somador_completo_2_p5, somador_completo_3_p5, somador_completo_4_p5,
       somador_completo_5_p5, somador_completo_6_p5, somador_completo_7_p5, xor_1_out, xor_2_out, xor_3_out,
       xor_4_out, xor_5_out, xor_6_out, xor_7_out, xor_8_out;

  xor xor_1 (xor_1_out, B0, M);
  xor xor_2 (xor_2_out, B1, M);
  xor xor_3 (xor_3_out, B2, M);
  xor xor_4 (xor_4_out, B3, M);
  // SOMADIMINUIR_somador_completo somador_completo_1: pin names not known; wires that end beside it: M, A0, xor_1_out, S0, somador_completo_1_p5
  // SOMADIMINUIR_somador_completo somador_completo_2: pin names not known; wires that end beside it: somador_completo_1_p5, A1, xor_2_out, S1, somador_completo_2_p5
  // SOMADIMINUIR_somador_completo somador_completo_3: pin names not known; wires that end beside it: somador_completo_2_p5, A2, xor_3_out, S2, somador_completo_3_p5
  // SOMADIMINUIR_somador_completo somador_completo_4: pin names not known; wires that end beside it: somador_completo_3_p5, A3, xor_4_out, S3, somador_completo_4_p5
  xor xor_5 (xor_5_out, B4, M);
  xor xor_6 (xor_6_out, B5, M);
  xor xor_7 (xor_7_out, B6, M);
  xor xor_8 (xor_8_out, B7, M);
  // SOMADIMINUIR_somador_completo somador_completo_5: pin names not known; wires that end beside it: somador_completo_4_p5, A4, xor_5_out, S4, somador_completo_5_p5
  // SOMADIMINUIR_somador_completo somador_completo_6: pin names not known; wires that end beside it: somador_completo_5_p5, A5, xor_6_out, S5, somador_completo_6_p5
  // SOMADIMINUIR_somador_completo somador_completo_7: pin names not known; wires that end beside it: somador_completo_6_p5, A6, xor_7_out, S6, somador_completo_7_p5
  // SOMADIMINUIR_somador_completo somador_completo_8: pin names not known; wires that end beside it: somador_completo_7_p5, A7, xor_8_out, S7, Cout
endmodule
