// Logisim project ep2.circ as structural Verilog: 13 circuits, main circuit main
module main (
  input  [7:0] A,
  input  [7:0] B,
  input  OP,
  output overflow__s_sinal,
  output overflow__c_sinal,
  output A_B__s_sinal,
  output A_B__s_sinal_2,
  output A_B,
  output A_0,
  output A_B__c_sinal,
  output A_B__c_sinal_2,
  output [7:0] R
);

  geral geral_1 (
    .A(A), .B(B), .OP(OP), .overflow_s__sinal(overflow__s_sinal), .A_B(A_B__s_sinal_2),
    .overflow_c_sinal(overflow__c_sinal), .A_B_3(A_B__s_sinal), .A_B_5(A_B), .R(R), .A_0(A_0),
    .A_B_2(A_B__c_sinal_2), .A_B_4(A_B__c_sinal));
endmodule

// ULA
module geral (
  input  [7:0] A,
  input  [7:0] B,
  input  OP,
  output overflow_s__sinal,
  output A_B,
  output A_B_2,
  output overflow_c_sinal,
  output A_B_3,
  output A_B_4,
  output A_0,
  output A_B_5,
  output [7:0] R
);

  somador_8bits somador_8bits_1 (
    .OP(OP), .Carry_sem_sinal(overflow_s__sinal), .Carry_com_sinal(overflow_c_sinal), .A(A), .B(B), .R(R));
  comp_magnitude__s_sinal comp_magnitude_s_sinal_1 (.A(A), .B(B), .A_B(A_B), .A_B_2(A_B_3), .A__B(A_B_5));
  comp_magnitude__c_sinal comp_magnitude_c_sinal_1 (.A(A), .B(B), .A_B(A_B_2), .A_B_2(A_B_4));  // open: A__B
  comp_zero comp_zero_1 (.A(A), .A__0(A_0));
endmodule

// comp. c/sinal
module comp_magnitude__c_sinal (
  input  [7:0] A,
  input  [7:0] B,
  output A_B,
  output A_B_2,
  output A__B
);

  comp_8bits__c_sinal comp_8bits_c_sinal_1 (
    .A_B(A_B), .A_B_2(A_B_2), .A__B(A__B), .A7(A[7]), .B7(B[7]), .A6(A[6]), .B6(B[6]), .A5(A[5]), .B5(B[5]),
    .A4(A[4]), .B4(B[4]), .A3(A[3]), .B3(B[3]), .A2(A[2]), .B2(B[2]), .A1(A[1]), .B1(B[1]), .A0(A[0]),
    .B0(B[0]));
endmodule

// comp. s/sinal
module comp_magnitude__s_sinal (
  input  [7:0] A,
  input  [7:0] B,
  output A_B,
  output A_B_2,
  output A__B
);

  comp_8bits__s_sinal comp_8bits_s_sinal_1 (
    .A_B(A_B), .A_B_2(A_B_2), .A__B(A__B), .A7(A[7]), .B7(B[7]), .A6(A[6]), .B6(B[6]), .A5(A[5]), .B5(B[5]),
    .A4(A[4]), .B4(B[4]), .A3(A[3]), .B3(B[3]), .A2(A[2]), .B2(B[2]), .A1(A[1]), .B1(B[1]), .A0(A[0]),
    .B0(B[0]));
endmodule

module comp_8bits__c_sinal (
  input  A7,
  input  B7,
  input  A6,
  input  B6,
  input  A5,
  input  B5,
  input  A4,
  input  B4,
  input  A3,
  input  B3,
  input  A2,
  input  B2,
  input  A1,
  input  B1,
  input  A0,
  input  B0,
  output A_B,
  output A_B_2,
  output A__B
);

  wire comp_magnitude_1bit_1_a__b, comp_magnitude_1bit_1_a_b, comp_magnitude_1bit_1_a_b_2,
       comp_magnitude_1bit_2_a__b, comp_magnitude_1bit_2_a_b, comp_magnitude_1bit_2_a_b_2,
       comp_magnitude_1bit_3_a__b, comp_magnitude_1bit_3_a_b, comp_magnitude_1bit_3_a_b_2,
       comp_magnitude_1bit_4_a__b, comp_magnitude_1bit_4_a_b, comp_magnitude_1bit_4_a_b_2,
       comp_magnitude_1bit_5_a__b, comp_magnitude_1bit_5_a_b, comp_magnitude_1bit_5_a_b_2,
       comp_magnitude_1bit_6_a__b, comp_magnitude_1bit_6_a_b, comp_magnitude_1bit_6_a_b_2,
       comp_magnitude_1bit_7_a__b, comp_magnitude_1bit_7_a_b, comp_magnitude_1bit_7_a_b_2,
       comp_magnitude_1bit_8_a_b, comp_magnitude_1bit_8_a_b_2, xor_1_out, xor_2_out;

  xor xor_1 (xor_1_out, 1'b1, A7);
  xor xor_2 (xor_2_out, B7, 1'b1);
  comp_magnitude_1bit comp_magnitude_1bit_1 (
    .habilitador(1'b1), .A(xor_1_out), .B(xor_2_out), .A__B(comp_magnitude_1bit_1_a__b),
    .A_B(comp_magnitude_1bit_1_a_b), .A_B_2(comp_magnitude_1bit_1_a_b_2));
  comp_magnitude_1bit comp_magnitude_1bit_2 (
    .habilitador(comp_magnitude_1bit_1_a__b), .A(A6), .B(B6), .A__B(comp_magnitude_1bit_2_a__b),
    .A_B(comp_magnitude_1bit_2_a_b), .A_B_2(comp_magnitude_1bit_2_a_b_2));
  comp_magnitude_1bit comp_magnitude_1bit_3 (
    .habilitador(comp_magnitude_1bit_2_a__b), .A(A5), .B(B5), .A__B(comp_magnitude_1bit_3_a__b),
    .A_B(comp_magnitude_1bit_3_a_b), .A_B_2(comp_magnitude_1bit_3_a_b_2));
  comp_magnitude_1bit comp_magnitude_1bit_4 (
    .habilitador(comp_magnitude_1bit_3_a__b), .A(A4), .B(B4), .A__B(comp_magnitude_1bit_4_a__b),
    .A_B(comp_magnitude_1bit_4_a_b), .A_B_2(comp_magnitude_1bit_4_a_b_2));
  comp_magnitude_1bit comp_magnitude_1bit_5 (
    .habilitador(comp_magnitude_1bit_4_a__b), .A(A3), .B(B3), .A__B(comp_magnitude_1bit_5_a__b),
    .A_B(comp_magnitude_1bit_5_a_b), .A_B_2(comp_magnitude_1bit_5_a_b_2));
  comp_magnitude_1bit comp_magnitude_1bit_6 (
    .habilitador(comp_magnitude_1bit_5_a__b), .A(A2), .B(B2), .A__B(comp_magnitude_1bit_6_a__b),
    .A_B(comp_magnitude_1bit_6_a_b), .A_B_2(comp_magnitude_1bit_6_a_b_2));
  comp_magnitude_1bit comp_magnitude_1bit_7 (
    .habilitador(comp_magnitude_1bit_6_a__b), .A(A1), .B(B1), .A__B(comp_magnitude_1bit_7_a__b),
    .A_B(comp_magnitude_1bit_7_a_b), .A_B_2(comp_magnitude_1bit_7_a_b_2));
  comp_magnitude_1bit comp_magnitude_1bit_8 (
    .habilitador(comp_magnitude_1bit_7_a__b), .A(A0), .B(B0), .A__B(A__B), .A_B(comp_magnitude_1bit_8_a_b),
    .A_B_2(comp_magnitude_1bit_8_a_b_2));
  or or_1 (A_B, comp_magnitude_1bit_8_a_b_2, comp_magnitude_1bit_7_a_b_2, comp_magnitude_1bit_6_a_b_2, comp_magnitude_1bit_5_a_b_2, comp_magnitude_1bit_4_a_b_2, comp_magnitude_1bit_3_a_b_2, comp_magnitude_1bit_2_a_b_2, comp_magnitude_1bit_1_a_b_2);
  or or_2 (A_B_2, comp_magnitude_1bit_8_a_b, comp_magnitude_1bit_7_a_b, comp_magnitude_1bit_6_a_b, comp_magnitude_1bit_5_a_b, comp_magnitude_1bit_4_a_b, comp_magnitude_1bit_3_a_b, comp_magnitude_1bit_2_a_b, comp_magnitude_1bit_1_a_b);
endmodule

module comp_8bits__s_sinal (
  input  A7,
  input  B7,
  input  A6,
  input  B6,
  input  A5,
  input  B5,
  input  A4,
  input  B4,
  input  A3,
  input  B3,
  input  A2,
  input  B2,
  input  A1,
  input  B1,
  input  A0,
  input  B0,
  output A_B,
  output A_B_2,
  output A__B
);

  wire comp_magnitude_1bit_1_a__b, comp_magnitude_1bit_1_a_b, comp_magnitude_1bit_1_a_b_2,
       comp_magnitude_1bit_2_a__b, comp_magnitude_1bit_2_a_b, comp_magnitude_1bit_2_a_b_2,
       comp_magnitude_1bit_3_a__b, comp_magnitude_1bit_3_a_b, comp_magnitude_1bit_3_a_b_2,
       comp_magnitude_1bit_4_a__b, comp_magnitude_1bit_4_a_b, comp_magnitude_1bit_4_a_b_2,
       comp_magnitude_1bit_5_a__b, comp_magnitude_1bit_5_a_b, comp_magnitude_1bit_5_a_b_2,
       comp_magnitude_1bit_6_a__b, comp_magnitude_1bit_6_a_b, comp_magnitude_1bit_6_a_b_2,
       comp_magnitude_1bit_7_a__b, comp_magnitude_1bit_7_a_b, comp_magnitude_1bit_7_a_b_2,
       comp_magnitude_1bit_8_a_b, comp_magnitude_1bit_8_a_b_2;

  comp_magnitude_1bit comp_magnitude_1bit_1 (
    .habilitador(1'b1), .A(A7), .B(B7), .A__B(comp_magnitude_1bit_1_a__b), .A_B(comp_magnitude_1bit_1_a_b),
    .A_B_2(comp_magnitude_1bit_1_a_b_2));
  comp_magnitude_1bit comp_magnitude_1bit_2 (
    .habilitador(comp_magnitude_1bit_1_a__b), .A(A6), .B(B6), .A__B(comp_magnitude_1bit_2_a__b),
    .A_B(comp_magnitude_1bit_2_a_b), .A_B_2(comp_magnitude_1bit_2_a_b_2));
  comp_magnitude_1bit comp_magnitude_1bit_3 (
    .habilitador(comp_magnitude_1bit_2_a__b), .A(A5), .B(B5), .A__B(comp_magnitude_1bit_3_a__b),
    .A_B(comp_magnitude_1bit_3_a_b), .A_B_2(comp_magnitude_1bit_3_a_b_2));
  comp_magnitude_1bit comp_magnitude_1bit_4 (
    .habilitador(comp_magnitude_1bit_3_a__b), .A(A4), .B(B4), .A__B(comp_magnitude_1bit_4_a__b),
    .A_B(comp_magnitude_1bit_4_a_b), .A_B_2(comp_magnitude_1bit_4_a_b_2));
  comp_magnitude_1bit comp_magnitude_1bit_5 (
    .habilitador(comp_magnitude_1bit_4_a__b), .A(A3), .B(B3), .A__B(comp_magnitude_1bit_5_a__b),
    .A_B(comp_magnitude_1bit_5_a_b), .A_B_2(comp_magnitude_1bit_5_a_b_2));
  comp_magnitude_1bit comp_magnitude_1bit_6 (
    .habilitador(comp_magnitude_1bit_5_a__b), .A(A2), .B(B2), .A__B(comp_magnitude_1bit_6_a__b),
    .A_B(comp_magnitude_1bit_6_a_b), .A_B_2(comp_magnitude_1bit_6_a_b_2));
  comp_magnitude_1bit comp_magnitude_1bit_7 (
    .habilitador(comp_magnitude_1bit_6_a__b), .A(A1), .B(B1), .A__B(comp_magnitude_1bit_7_a__b),
    .A_B(comp_magnitude_1bit_7_a_b), .A_B_2(comp_magnitude_1bit_7_a_b_2));
  comp_magnitude_1bit comp_magnitude_1bit_8 (
    .habilitador(comp_magnitude_1bit_7_a__b), .A(A0), .B(B0), .A__B(A__B), .A_B(comp_magnitude_1bit_8_a_b),
    .A_B_2(comp_magnitude_1bit_8_a_b_2));
  or or_1 (A_B, comp_magnitude_1bit_8_a_b_2, comp_magnitude_1bit_7_a_b_2, comp_magnitude_1bit_6_a_b_2, comp_magnitude_1bit_5_a_b_2, comp_magnitude_1bit_4_a_b_2, comp_magnitude_1bit_3_a_b_2, comp_magnitude_1bit_2_a_b_2, comp_magnitude_1bit_1_a_b_2);
  or or_2 (A_B_2, comp_magnitude_1bit_8_a_b, comp_magnitude_1bit_7_a_b, comp_magnitude_1bit_6_a_b, comp_magnitude_1bit_5_a_b, comp_magnitude_1bit_4_a_b, comp_magnitude_1bit_3_a_b, comp_magnitude_1bit_2_a_b, comp_magnitude_1bit_1_a_b);
endmodule

module comp_magnitude_1bit (
  input  habilitador,
  input  A,
  input  B,
  output A__B,
  output A_B,
  output A_B_2
);

  wire not_1_out, not_2_out, not_3_out, xor_1_out;

  xor xor_1 (xor_1_out, A, B);
  not not_1 (not_1_out, xor_1_out);
  and and_1 (A_B, habilitador, A, not_2_out);
  not not_2 (not_2_out, B);
  and and_2 (A_B_2, habilitador, not_3_out, B);
  not not_3 (not_3_out, A);
  and and_3 (A__B, habilitador, not_1_out);
endmodule

// comp. zero
module comp_zero (
  input  [7:0] A,
  output A__0
);

  comp_zero_8bits comp_zero_8bits_1 (
    .A7(A[7]), .A6(A[6]), .A5(A[5]), .A4(A[4]), .A3(A[3]), .A2(A[2]), .A1(A[1]), .A0(A[0]), .A__0(A__0));
endmodule

module comp_zero_8bits (
  input  A7,
  input  A6,
  input  A5,
  input  A4,
  input  A3,
  input  A2,
  input  A1,
  input  A0,
  output A__0
);

  wire comp_zero_1bit_1_a__0, comp_zero_1bit_2_a__0, comp_zero_1bit_3_a__0, comp_zero_1bit_4_a__0,
       comp_zero_1bit_5_a__0, comp_zero_1bit_6_a__0, comp_zero_1bit_7_a__0;

  comp_zero_1bit comp_zero_1bit_1 (.habilitador(1'b1), .A(A7), .A__0(comp_zero_1bit_1_a__0));
  comp_zero_1bit comp_zero_1bit_2 (.habilitador(comp_zero_1bit_1_a__0), .A(A6), .A__0(comp_zero_1bit_2_a__0));
  comp_zero_1bit comp_zero_1bit_3 (.habilitador(comp_zero_1bit_2_a__0), .A(A5), .A__0(comp_zero_1bit_3_a__0));
  comp_zero_1bit comp_zero_1bit_4 (.habilitador(comp_zero_1bit_3_a__0), .A(A4), .A__0(comp_zero_1bit_4_a__0));
  comp_zero_1bit comp_zero_1bit_5 (.habilitador(comp_zero_1bit_4_a__0), .A(A3), .A__0(comp_zero_1bit_5_a__0));
  comp_zero_1bit comp_zero_1bit_6 (.habilitador(comp_zero_1bit_5_a__0), .A(A2), .A__0(comp_zero_1bit_6_a__0));
  comp_zero_1bit comp_zero_1bit_7 (.habilitador(comp_zero_1bit_6_a__0), .A(A1), .A__0(comp_zero_1bit_7_a__0));
  comp_zero_1bit comp_zero_1bit_8 (.habilitador(comp_zero_1bit_7_a__0), .A(A0), .A__0(A__0));
endmodule

module comp_zero_1bit (
  input  habilitador,
  input  A,
  output A__0
);

  wire not_1_out, xor_1_out;

  xor xor_1 (xor_1_out, A, 1'b0);
  not not_1 (not_1_out, xor_1_out);
  and and_1 (A__0, habilitador, not_1_out);
endmodule

// somador
module somador_8bits (
  input  [7:0] A,
  input  [7:0] B,
  input  OP,
  output Carry_sem_sinal,
  output [7:0] R,
  output Carry_com_sinal
);

  wire somador_1_c7, somador_1_c8;

  somador somador_1 (
    .a0(A[0]), .a1(A[1]), .a2(A[2]), .a3(A[3]), .a4(A[4]), .a5(A[5]), .a6(A[6]), .a7(A[7]), .b0(B[0]),
    .b1(B[1]), .b2(B[2]), .b3(B[3]), .b4(B[4]), .b5(B[5]), .b6(B[6]), .b7(B[7]), .c7(somador_1_c7), .c0(OP),
    .c8(somador_1_c8), .s0(R[0]), .s1(R[1]), .s2(R[2]), .s3(R[3]), .s4(R[4]), .s5(R[5]), .s6(R[6]), .s7(R[7]));
  xor xor_1 (Carry_sem_sinal, OP, somador_1_c8);
  xor xor_2 (Carry_com_sinal, somador_1_c7, somador_1_c8);
endmodule

module somador (
  input  a0,
  input  b0,
  input  a1,
  input  b1,
  input  a2,
  input  b2,
  input  a3,
  input  b3,
  input  a4,
  input  b4,
  input  a5,
  input  b5,
  input  a6,
  input  b6,
  input  a7,
  input  b7,
  input  c0,
  output c7,
  output c8,
  output s0,
  output s1,
  output s2,
  output s3,
  output s4,
  output s5,
  output s6,
  output s7
);

  wire somabits_1_cout, somabits_2_cout, somabits_3_cout, somabits_4_cout, somabits_5_cout, somabits_6_cout,
       xor_1_out, xor_2_out, xor_3_out, xor_4_out, xor_5_out, xor_6_out, xor_7_out, xor_8_out;

  xor xor_1 (xor_1_out, c0, b0);
  somabits somabits_1 (.Cin(c0), .Cout(somabits_1_cout), .A(a0), .B(xor_1_out), .S(s0));
  xor xor_2 (xor_2_out, c0, b1);
  somabits somabits_2 (.Cin(somabits_1_cout), .Cout(somabits_2_cout), .A(a1), .B(xor_2_out), .S(s1));
  xor xor_3 (xor_3_out, c0, b2);
  somabits somabits_3 (.Cin(somabits_2_cout), .Cout(somabits_3_cout), .A(a2), .B(xor_3_out), .S(s2));
  xor xor_4 (xor_4_out, c0, b3);
  somabits somabits_4 (.Cin(somabits_3_cout), .Cout(somabits_4_cout), .A(a3), .B(xor_4_out), .S(s3));
  xor xor_5 (xor_5_out, c0, b4);
  somabits somabits_5 (.Cin(somabits_4_cout), .Cout(somabits_5_cout), .A(a4), .B(xor_5_out), .S(s4));
  xor xor_6 (xor_6_out, c0, b5);
  somabits somabits_6 (.Cin(somabits_5_cout), .Cout(somabits_6_cout), .A(a5), .B(xor_6_out), .S(s5));
  xor xor_7 (xor_7_out, c0, b6);
  somabits somabits_7 (.Cin(somabits_6_cout), .Cout(c7), .A(a6), .B(xor_7_out), .S(s6));
  xor xor_8 (xor_8_out, c0, b7);
  somabits somabits_8 (.Cin(c7), .Cout(c8), .A(a7), .B(xor_8_out), .S(s7));

  // Notes on the sheet:
  //   S
endmodule

module somabits (
  input  A,
  input  B,
  input  Cin,
  output Cout,
  output S
);

  wire and_1_out, nor_1_out, not_1_out, xor_1_out;

  xor xor_1 (xor_1_out, A, B);
  xor xor_2 (S, xor_1_out, Cin);
  nor nor_1 (nor_1_out, B, A, Cin);
  and and_1 (and_1_out, B, A, Cin);
  not not_1 (not_1_out, S);
  ExactlyOne xor_3 (.out(Cout), .in0(not_1_out), .in1(nor_1_out), .in2(and_1_out));
endmodule
